# Fritzing sketch Proj1Sketch (saved by Fritzing 0.9.3b)
breadboards: 1

parts:
  Part1 = Arduino Uno (Rev3)
  hc-sr1 = hc-sr04
  hc-sr2 = hc-sr04

nets:
  N1: Part1.D9_PWM, hc-sr1.Trig
  N2: Part1.D10_PWM/SS, hc-sr1.Echo
  N3: Part1.D11_PWM/MOSI, hc-sr2.Trig
  N4: Part1.D12/MISO, hc-sr2.Echo
  VCC: Part1.5V, hc-sr1.VCC, hc-sr2.VCC
  GND: Part1.GND, hc-sr1.GND, hc-sr2.GND
